# Fritzing sketch PlantWatering (saved by Fritzing 0.9.4)
breadboards: 1

parts:
  Argon1 = Particle Argon
  Relay1 = Relay - 6 pins [package="DIP (Dual Inline) [THT]"]
  OLED_I2C1 = OLED 128x64 I2C Monochrome Display
  Grove1 = Grove Dust Sensor
  Part1 = MQ-131 breakout
  Q1 = PNP-Transistor [package="TO92 [THT]"]
  R1 = Resistor [tolerance=±5% resistance=220 package=THT]
  R2 = Resistor [tolerance=±5% resistance=220 package=THT]
  M1 = DC Motor
  S1 = Pushbutton [package="[THT]"]
  M2 = BMP280
  SENS1 = SoilWatch 10
  Water_Level_Sensor1 = Water Level Sensor

nets:
  VCC: Argon1.3.3V, Relay1.VCC, Relay1.ON, OLED_I2C1.VDD, Grove1.VCC, Part1.VCC, M2.VIN, SENS1.VCC, Water_Level_Sensor1.VCC
  GND: Argon1.GND, Relay1.GND, OLED_I2C1.GND, Grove1.GND, Part1.GND, Q1.C, R2.Pin_0, M1.pin_2, S1.Pin_3, S1.Pin_4, M2.GND, SENS1.GND, Water_Level_Sensor1.GND
  N1: Argon1.A0, Part1.AO
  N2: Argon1.A1, SENS1.OUT
  N3: Argon1.A2, Water_Level_Sensor1.SIG
  N4: Argon1.A3, Grove1.SIG
  N5: Argon1.A4, Q1.B, R2.Pin_1
  N6: Argon1.SDA, OLED_I2C1.SDA, M2.SDA
  N7: Argon1.SCL, OLED_I2C1.SCK, M2.SCL
  N8: Argon1.D6, S1.Pin_1, S1.Pin_2
  N9: Argon1.D8, Part1.DO
  N10: Argon1.VUSB, R1.Pin_0
  N11: Relay1.IN, Q1.E, R1.Pin_1
  N12: Relay1.COM, M1.pin_1

custom parts:
  Particle Argon: The Argon is a powerful Wi-Fi enabled development board that can act as either a standalone Wi-Fi endpoint or Wi-Fi enabled gateway for Particle Mesh networks. It is based on the Nordic nRF52840 and has built-in battery charging circuitry so it’s easy to connect a Li-Po and deploy your local network in minutes. The Argon is great for connecting existing projects to the Particle Device Cloud or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
  Relay - 6 pins: A DIP stand-in part for whatever IC you want. With 6 pins on a 900mil dual inline package (DIP) footprint.
  Grove Dust Sensor: PPD42 Grove Dust Sensor
  MQ-131 breakout: SKU: 101282
  Pushbutton: A generic pushbutton.
  BMP280: Temperature Humidity Barometric presure Sensor, I2C
  SoilWatch 10: SoilWatch 10 - Capacitive soil moisture sensor
  Water Level Sensor: A water level sensor. This sensor operates at 3V to 5V. The Sig (signal) pin outputs an analogue signal that is in proportion to the amount of water in contact with the sensor.
